# Fritzing sketch ConexionBluetoothMega (saved by Fritzing 0.9.3b)

parts:
  Componente1 = Bluetooth HC-05 Macho
  Componente2 = Arduino Mega 2560 (Rev3)

nets:
  N1: Componente1.TXD, Componente2.D19/RX1
  N2: Componente1.RXD, Componente2.D18/TX1
  VCC: Componente1.VCC, Componente2.5V
  GND: Componente1.GND, Componente2.GND
