# Fritzing sketch 2 displays conecction to arduino (saved by Fritzing 0.8.7b)
breadboards: 1

parts:
  Parte1 = Arduino Mega 2560 (Rev3)
  7_Segment1 = 7 Segment Display
  7_Segment2 = 7 Segment Display
  R1 = Resistor [tolerance=±5% resistance=220 package=THT]
  R2 = Resistor [tolerance=±5% resistance=220 package=THT]
  R3 = Resistor [tolerance=±5% resistance=220 package=THT]
  R4 = Resistor [tolerance=±5% resistance=220 package=THT]

nets:
  N1: Parte1.GND, R1.Pin_0, R2.Pin_1, R3.Pin_1, R4.Pin_0
  N2: Parte1.D39, 7_Segment2.Segment_A
  N3: Parte1.D40, 7_Segment2.Segment_B
  N4: Parte1.D41, 7_Segment2.Segment_C
  N5: Parte1.D42, 7_Segment2.Segment_D
  N6: Parte1.D43, 7_Segment2.Segment_E
  N7: Parte1.D44, 7_Segment2.Segment_F
  N8: Parte1.D45, 7_Segment2.Segment_G
  N9: Parte1.D46, 7_Segment1.Segment_A
  N10: Parte1.D47, 7_Segment1.Segment_B
  N11: Parte1.D48, 7_Segment1.Segment_C
  N12: Parte1.D49, 7_Segment1.Segment_D
  N13: Parte1.D50, 7_Segment1.Segment_E
  N14: Parte1.D51, 7_Segment1.Segment_F
  N15: Parte1.D52, 7_Segment1.Segment_G
  N16: 7_Segment1.common_anode, R3.Pin_0, R4.Pin_1
  N17: 7_Segment2.common_anode, R1.Pin_1, R2.Pin_0

notes:
  Esquematico realizado por:
  Video Tutoriales Tostatronic
  Facebook: Tostatronic
  Pagina WEB: www.tostratonic.com
  Cel: 3314575853
